# Fritzing sketch GPSwristband (saved by Fritzing 0.9.2b)
breadboards: 1

parts:
  Part1 = Arduino Pro Mini v13  # not connected
  U1 = LIPO-110mAh [package=lipo-110]  # not connected
  Part2 = Power Cell LiPo Charger/Booster  # not connected
  Part3 = Arduino Uno (Rev3)
  Part5 = Bluetooth Mate Silver  # not connected
  LED2 = RGB LED (com. cathode, rbg) [package="5 mm [THT]"]
  LED3 = RGB LED (com. cathode, rbg) [package="5 mm [THT]"]

nets:
  N1: Part3.D8, LED2.green_anode, LED3.green_anode
  N2: Part3.D9_PWM, LED2.blue_anode, LED3.blue_anode
  N3: Part3.D10_PWM/SS, LED2.red_anode, LED3.red_anode
  N4: Part3.GND, LED2.common_cathode, LED3.common_cathode
