# Fritzing sketch final_schematic (saved by Fritzing 0.9.2b)
breadboards: 1

parts:
  Part2 = PowerBoost 500 Charger
  U1 = LIPO-1000mAh [package=lipo-1000]
  GPS1 = Adafruit Ultimate GPS Breakout
  Part3 = Arduino Pro Mini v13
  Part4 = FTDI Basic Programmer
  microSD1 = MicroSD Breakout
  U3 = microSD Socket [package=micro-sd-socket-pp]  # not connected
  BLUEFRUIT1 = Adafruit Bluefruit EZ-LINK v1.0
  LED1 = RGB LED (com. cathode, rgb) [package="5 mm [THT]"]
  S1 = Pushbutton [package="[THT]"]
  S2 = Pushbutton [package="[THT]"]
  R1 = Resistor [tolerance=±5% resistance=10k package=THT]
  R2 = Resistor [tolerance=±5% resistance=10k package=THT]  # not connected
  S3 = Toggle Switch [package=THT]

nets:
  N1: Part2.VBAT, S3.COM
  GND: Part2.GND, U1.-, GPS1.GND, microSD1.GND, BLUEFRUIT1.GND, R1.Pin_0
  VIN: Part2.5.0V, GPS1.VIN, microSD1.5V, LED1.common_cathode, R1.Pin_1
  N2: U1.+, S3.L1
  3.3V: GPS1.3.3V, BLUEFRUIT1.Vin
  N3: GPS1.TX, Part3.D3_PWM
  N4: GPS1.RX, Part3.D2
  N5: Part3.DTR, Part4.DTR
  N6: Part3.D0/TX, Part4.RXI, BLUEFRUIT1.RX
  N7: Part3.D1/RX, Part4.TXO, BLUEFRUIT1.TX
  N8: Part3.VCC, Part4.POWER
  GND_2: Part3.GND, Part4.CTS, Part4.GND
  N9: Part3.A2, LED1.blue_anode
  N10: Part3.A0, LED1.red_anode
  N11: Part3.D13/SCK, microSD1.DO
  N12: Part3.D12/MISO, microSD1.DI
  N13: Part3.D11_PWM/MOSI, microSD1.CS
  N14: Part3.D10_PWM/SS, microSD1.CD
  N15: S1.Pin_1, S1.Pin_2
  N16: S1.Pin_3, S1.Pin_4
  N17: S2.Pin_1, S2.Pin_2
  N18: S2.Pin_3, S2.Pin_4

custom parts:
  PowerBoost 500 Charger: The PowerBoost 500C is a little DC/DC boost converter module that can be powered by any 3.7V LiIon/LiPoly battery, and convert the battery output to 5.2V DC for running your 5V projects. At its heart is a TPS61090 boost converter from TI. This boost converter chip has some really nice extras such as low battery detection, 2A internal switch, synchronous conversion, excellent efficiency, and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
  MicroSD Breakout: 5V-ready microSD Breakout with Level Shifter
  Adafruit Bluefruit EZ-LINK v1.0: Bluefruit EZ-LINK, Bluetooth Serial Link & Arduino Programmer
